# Fritzing sketch scheme (saved by Fritzing 0.9.3b)
breadboards: 1

parts:
  WeMos_D1_Mini1 = WeMos D1 Mini
  Часть1 = ws2812b [package="smd 2812b"]
  S1 = TILT-SWITCH-SW-200D [package=reed_switch_plastic]
  S2 = TILT-SWITCH-SW-200D [package=reed_switch_plastic]
  R1 = Resistor [tolerance=±5% resistance=10k package=THT]
  R2 = Resistor [tolerance=±5% resistance=10k package=THT]
  U1 = RELAY [package=relay-t9a-2]
  U2 = RELAY [package=relay-t9a-2]
  DS18B20 = TEMPERATURE-SENSOR [package=to-92]
  R3 = Resistor [tolerance=±5% resistance=4.7k package=THT]
  PIR = PIR sensor

nets:
  N1: WeMos_D1_Mini1.3V3, R1.Pin_0, R2.Pin_0
  VDD: WeMos_D1_Mini1.5V, Часть1.VDD, PIR.VDD
  N2: WeMos_D1_Mini1.D1, U1.COIL1
  N3: WeMos_D1_Mini1.D2, S2.1, R2.Pin_1
  N4: WeMos_D1_Mini1.D3, S1.1
  N5: WeMos_D1_Mini1.D4, Часть1.DIN
  N6: WeMos_D1_Mini1.D5, PIR.SIG
  N7: WeMos_D1_Mini1.D6, U2.COIL1
  N8: WeMos_D1_Mini1.D8, DS18B20.ADJ, R3.Pin_0
  GND: WeMos_D1_Mini1.G, Часть1.VSS, S1.2, S2.2, DS18B20.GND, PIR.GND
  N9: U1.COIL2, U2.COIL2
  N10: DS18B20.VCC, R3.Pin_1
